// Logisim project Clock_Module.circ as structural Verilog
module Clock_Module (
  input  HLT,
  output CLK
);

  wire clock_1_out, not_1_out;

  Clock clock_1 (.out(clock_1_out));
  not not_1 (not_1_out, HLT);
  and and_1 (CLK, clock_1_out, not_1_out);

  // Notes on the sheet:
  //   Clock Module
endmodule

module _8_bit_register (
  input  CLK,
  input  D,
  output Q,
  output Q_prime
);

  wire and_1_out, and_2_out, and_3_out, not_1_out, not_2_out, not_3_out, not_4_out;

  not not_1 (not_1_out, CLK);
  not not_2 (not_2_out, not_1_out);
  not not_3 (not_3_out, not_2_out);
  and and_1 (and_1_out, CLK, not_3_out);
  not not_4 (not_4_out, D);
  and and_2 (and_2_out, not_4_out, and_1_out);
  and and_3 (and_3_out, and_1_out, D);
  nor nor_1 (Q, and_2_out, Q_prime);
  nor nor_2 (Q_prime, Q, and_3_out);

  // Notes on the sheet:
  //   S
  //   Q
  //   Q'
endmodule

module _8_BIT_REGISTER (
  input  CLK,
  input  LOAD_prime,
  input  D,
  output out_4
);

  wire and_1_out, and_2_out, not_1_out, or_1_out;

  not not_1 (not_1_out, LOAD_prime);
  and and_1 (and_1_out, out_4, LOAD_prime);
  and and_2 (and_2_out, not_1_out, D);
  or or_1 (or_1_out, and_1_out, and_2_out);
  // _8_bit_register 8_bit_register_1: pin names not known; wires that end beside it: CLK, or_1_out, out_4
endmodule

module _8_1BIT_REGISTER (
  input  CLK,
  input  LOAD_prime,
  input  _1D,
  input  _2D,
  input  _3D,
  input  _4D,
  input  _5D,
  input  _6D,
  input  _7D,
  input  _8D,
  output _1Q,
  output _2Q,
  output _3Q,
  output _4Q,
  output _5Q,
  output _6Q,
  output _7Q,
  output _8Q
);

  // _8_BIT_REGISTER 8_bit_register_1: pin names not known; wires that end beside it: CLK, LOAD_prime, _1D, _1Q
  // _8_BIT_REGISTER 8_bit_register_2: pin names not known; wires that end beside it: CLK, LOAD_prime, _2D, _2Q
  // _8_BIT_REGISTER 8_bit_register_3: pin names not known; wires that end beside it: CLK, LOAD_prime, _3D, _3Q
  // _8_BIT_REGISTER 8_bit_register_4: pin names not known; wires that end beside it: CLK, LOAD_prime, _4D, _4Q
  // _8_BIT_REGISTER 8_bit_register_5: pin names not known; wires that end beside it: CLK, LOAD_prime, _5D, _5Q
  // _8_BIT_REGISTER 8_bit_register_6: pin names not known; wires that end beside it: CLK, LOAD_prime, _6D, _6Q
  // _8_BIT_REGISTER 8_bit_register_7: pin names not known; wires that end beside it: CLK, LOAD_prime, _7D, _7Q
  // _8_BIT_REGISTER 8_bit_register_8: pin names not known; wires that end beside it: CLK, LOAD_prime, _8D, _8Q
endmodule

module OUTPUT_BUFFER (
  input  _1q,
  input  _2q,
  input  _3q,
  input  _4q,
  input  _5q,
  input  _6q,
  input  _7q,
  input  _8q,
  input  EN_prime,
  output _1d,
  output _2d,
  output _3d,
  output _4d,
  output _5d,
  output _6d,
  output _7d,
  output _8d
);

  wire not_1_out;

  not not_1 (not_1_out, EN_prime);
  assign _1d = not_1_out ? _1q : 1'bz;  // Controlled_Buffer controlled_buffer_1
  assign _2d = not_1_out ? _2q : 1'bz;  // Controlled_Buffer controlled_buffer_2
  assign _3d = not_1_out ? _3q : 1'bz;  // Controlled_Buffer controlled_buffer_3
  assign _4d = not_1_out ? _4q : 1'bz;  // Controlled_Buffer controlled_buffer_4
  assign _5d = not_1_out ? _5q : 1'bz;  // Controlled_Buffer controlled_buffer_5
  assign _6d = not_1_out ? _6q : 1'bz;  // Controlled_Buffer controlled_buffer_6
  assign _7d = not_1_out ? _7q : 1'bz;  // Controlled_Buffer controlled_buffer_7
  assign _8d = not_1_out ? _8q : 1'bz;  // Controlled_Buffer controlled_buffer_8
endmodule
